# Fritzing sketch sailing-start (saved by Fritzing 0.9.3b)
perfboards: 1

parts:
  Part1 = Arduino Micro (Rev3)
  R1 = Resistor [tolerance=±5% resistance=100 package="2512 [SMD]"]
  Grove1 = Grove 4 Digit Display
  R3 = Resistor [tolerance=±5% resistance=100 package="2512 [SMD]"]
  R4 = Resistor [tolerance=±5% resistance=100 package="2512 [SMD]"]
  S4 = SWITCH-DPDT [package=ayz0202]
  S5 = Round Pushbutton
  S6 = Round Pushbutton
  R5 = Resistor [tolerance=±5% resistance=100 package="2512 [SMD]"]
  U1 = RELAY [package=relay-g5q]
  SPKR1 = Loudspeaker
  U2 = BATTERY-2 [package=battery-aaa]
  U3 = BATTERY-2 [package=battery-aaa]
  U4 = BATTERY-2 [package=battery-aaa]

nets:
  GND: Part1.GND, R1.Pin_1, Grove1.GND, R3.Pin_1, R4.Pin_1, R5.Pin_1
  5V: Part1.5V, Grove1.VCC, S4.1, S4.4, S5.leg1, S6.leg1, U1.COIL2
  N1: Part1.A5, Grove1.CLK
  N2: Part1.A4, Grove1.DIO
  N3: Part1.A3, R3.Pin_0, S4.5
  N4: Part1.A2, S4.2, R5.Pin_0
  N5: Part1.A1, R1.Pin_0, S6.leg0
  N6: Part1.A0, R4.Pin_0, S5.leg0
  N7: Part1.D13_PWM, U1.COIL1
  N8: U1.MAIN, U2.+1, U3.+1, U4.+1
  N9: U1.NC, SPKR1.pin2
  N10: SPKR1.pin1, U2.-1, U3.-1, U4.-1

// code stored in the sketch: Button.ino
/*
  Button
 
 Turns on and off a light emitting diode(LED) connected to digital  
 pin 13, when pressing a pushbutton attached to pin 2. 
 
 
 The circuit:
 * LED attached from pin 13 to ground 
 * pushbutton attached to pin 2 from +5V
 * 10K resistor attached to pin 2 from ground
 
 * Note: on most Arduinos there is already an LED on the board
 attached to pin 13.
 
 
 created 2005
 by DojoDave <http://www.0j0.org>
 modified 30 Aug 2011
 by Tom Igoe
 
 This example code is in the public domain.
 
 http://www.arduino.cc/en/Tutorial/Button
 */

// constants won't change. They're used here to 
// set pin numbers:
const int buttonPin = 2;     // the number of the pushbutton pin
const int ledPin =  13;      // the number of the LED pin

// variables will change:
int buttonState = 0;         // variable for reading the pushbutton status

void setup() {
  // initialize the LED pin as an output:
  pinMode(ledPin, OUTPUT);      
  // initialize the pushbutton pin as an input:
  pinMode(buttonPin, INPUT);     
}

void loop(){
  // read the state of the pushbutton value:
  buttonState = digitalRead(buttonPin);

  // check if the pushbutton is pressed.
  // if it is, the buttonState is HIGH:
  if (buttonState == HIGH) {     
    // turn LED on:    
    digitalWrite(ledPin, HIGH);  
  } 
  else {
    // turn LED off:
    digitalWrite(ledPin, LOW); 
  }
}
